// Logisim project cpu.circ as structural Verilog: 1 circuit, main circuit cpu
module cpu (
  input  clk,
  input  [31:0] INSTRUCTION,
  input  [31:0] READ_DATA,
  output [31:0] WRITE_ADDRESS,
  output [31:0] PROGRAM_COUNTER,
  output [31:0] ra,
  output [31:0] sp,
  output [31:0] t0,
  output [31:0] t1,
  output [31:0] t2,
  output [31:0] s0,
  output [31:0] s1,
  output [31:0] a0,
  output [31:0] tohost,
  output [3:0] WRITE_ENABLE,
  output [31:0] WRITE_DATA
);

  wire RegWEn;
  wire [31:0] adder_1_out, alu_result, gen_imm, read_data_1, read_data_2, write_data_t;

  Adder #(.width(32)) adder_1 (.a(PROGRAM_COUNTER), .b(32'h4), .out(adder_1_out));  // open: cin, cout
  Register #(.width(32)) PC (.D(adder_1_out), .clk(clk), .Q(PROGRAM_COUNTER));  // open: en, clr
  control_logic control_logic_1 (.RegWEn(RegWEn));  // open: CSRWen, PCSel, ImmSel, BrUn, ASel, BSel, ALUSel, MemRW, WBSel, CSRSel, inst, BrEq, BrLt
  imm_gen imm_gen_1 (.inst(INSTRUCTION), .ImmSel(3'b100), .imm(gen_imm));
  regfile regfile_1 (
    .rs1(INSTRUCTION[19:15]), .rd(INSTRUCTION[11:7]), .Write_Data(write_data_t), .RegWEn(RegWEn), .clk(clk),
    .ra(ra), .sp(sp), .t0(t0), .t1(t1), .t2(t2), .s0(s0), .s1(s1), .a0(a0), .Read_Data_1(read_data_1),
    .Read_Data_2(read_data_2));  // open: rs2
  // branch_comp branch_comp_1: pin names not known
  csr csr_1 (.tohost(tohost));  // open: CSR_address, CSR_din, CSR_WE, clk
  alu alu_1 (.Result(alu_result), .A(read_data_1), .B(gen_imm), .ALUSel(4'b0000));
  Multiplexer #(.enable("false"), .select(2), .width(32)) multiplexer_1 (
    .in0(read_data_1), .in1(alu_result), .out(write_data_t), .sel(2'b01));  // open: in2, in3

  // Other names for the same wires on the sheet: opcode[6:0] = INSTRUCTION[6:0]; rd[4:0] = INSTRUCTION[11:7];
  //   funct3[2:0] = INSTRUCTION[14:12]; rs1[4:0] = INSTRUCTION[19:15]; imm[11:0] = INSTRUCTION[31:20]

  // Notes on the sheet:
  //   Output to IMEM
  //   IMEM (do **NOT** move this)
  //   Inputs from IMEM
  //   Inputs/Outputs for testing. Do **NOT** move these.
  //   Outputs To DMEM
  //   DMEM (do **NOT** move this)
  //   Inputs From DMEM
endmodule
